# Fritzing sketch LCD-Stepper-Vend (saved by Fritzing 0.8.3b)
breadboards: 1

parts:
  Part2 = Arduino Uno (Rev3)
  J2 = Basic Servo
  BAT2 = BC9VPC [package=bc9vpc]
  TRS2 = Audio Jack (TRS) 3.5mm [package="4Ucon 08780 [THT]"]
  IC2 = IC, DIP package, 16 pins [chip_label=WTV020 part_number=WTV020]
  SP2 = SPEAKER [package=pcb_mount_speaker]  # not connected
  R3 = Resistor [tolerance=±5% resistance=220 package=THT]
  LED2 = LED - 5mm [color="Yellow (595nm)" package="5 mm [THT]"]

nets:
  GND: Part2.GND, J2.gnd, BAT2.V+, IC2.pin8
  N1: Part2.D9_PWM, J2.pulse
  N2: Part2.D3_PWM, IC2.pin7
  N3: Part2.D6_PWM, IC2.pin10
  N4: Part2.D7, IC2.pin15, LED2.cathode
  N5: Part2.3V3, R3.Pin_1
  N6: J2.vcc, BAT2.V-
  N7: TRS2.Ring, TRS2.Tip, IC2.pin4, IC2.pin5
  N8: R3.Pin_0, LED2.anode

notes:
  Handle 2
  to 'Earth'
  Handle 1
  to 'Click'
  Pretend this is your Webcam
  Pretend this is your PC
  USB - USB - USB
  Pretend this is your
  MAKEY MAKEY
  pin 14
